// Digital circuit ALU.dig as structural Verilog
module ALU (
  input  OpA,
  input  OpB,
  input  OpC,
  input  [7:0] A,
  input  [7:0] B,
  output [7:0] Out,
  output out_7,
  output overFlow,
  output a_lt_b,
  output b_lt_a,
  output eq
);

  wire opcode_1__0, opcode_1__1, opcode_1__2, sub8bit_1_cout, sum8bit_1_cout;
  wire [7:0] bitshift_1_p2, multiplier4bit_1_o8bit, sub8bit_1_o, sum8bit_1_o;

  sub8bit sub8bit_1 (.C(1'b0), .A(A), .B(B), .Cout(sub8bit_1_cout), .O(sub8bit_1_o));
  sum8bit sum8bit_1 (.C(1'b0), .A(A), .B(B), .Cout(sum8bit_1_cout), .O(sum8bit_1_o));
  // bitShift bitshift_1: pin names not known; wires that end beside it: A, bitshift_1_p2
  multiplier4bit multiplier4bit_1 (.A4bit(A), .B4bit(B), .O8bit(multiplier4bit_1_o8bit));
  comparador8bit comparador8bit_1 (
    .CoutSub(sub8bit_1_cout), .OutSub8bit(sub8bit_1_o), .a_lt_b(a_lt_b), .b_lt_a(b_lt_a), .eq(eq));
  assign overFlow = opcode_1__0 ? sum8bit_1_cout : 1'bz;  // Driver driver_1
  assign Out = out_7 ? bitshift_1_p2 : 8'bz;  // Driver driver_2
  assign out_7 = opcode_1__1 ? sub8bit_1_cout : 1'bz;  // Driver driver_3
  assign Out = opcode_1__2 ? multiplier4bit_1_o8bit : 8'bz;  // Driver driver_4
  assign Out = opcode_1__1 ? sub8bit_1_o : 8'bz;  // Driver driver_5
  assign Out = opcode_1__0 ? sum8bit_1_o : 8'bz;  // Driver driver_6
  opcode opcode_1 (
    .A(OpA), .B(OpB), .C(OpC), ._0(opcode_1__0), ._1(opcode_1__1), ._2(opcode_1__2), ._3(out_7));  // open: _4
endmodule
