// Digital circuit CPU.dig as structural Verilog
module CPU (
  input  [7:0] A,
  input  [7:0] B,
  input  Clock,
  input  [2:0] read,
  input  [2:0] \operação ,
  input  [2:0] write,
  output [7:0] Out
);

  wire alu_1_a_lt_b, alu_1_b_lt_a, alu_1_eq, alu_1_out_7, alu_1_overflow, and_1_out, and_2_out, and_3_out,
       and_4_out, and_5_out, opcode_1__0, opcode_1__1, opcode_1__2, opcode_1__3, opcode_1__4, opcode_2__0,
       opcode_2__1, opcode_2__2, opcode_2__3, opcode_2__4;
  wire [7:0] alu_1_out, registrador8bit_1_out, registrador8bit_2_out, registrador8bit_3_out,
       registrador8bit_4_out, registrador8bit_5_out;

  opcode opcode_1 (
    .A(read[0]), .B(read[1]), .C(read[2]), ._0(opcode_1__0), ._1(opcode_1__1), ._2(opcode_1__2),
    ._3(opcode_1__3), ._4(opcode_1__4));
  ALU alu_1 (
    .OpA(\operação [0]), .OpB(\operação [1]), .OpC(\operação [2]), .A(A), .B(B), .Out(alu_1_out),
    .out_7(alu_1_out_7), .overFlow(alu_1_overflow), .a_lt_b(alu_1_a_lt_b), .b_lt_a(alu_1_b_lt_a),
    .eq(alu_1_eq));
  opcode opcode_2 (
    .A(write[0]), .B(write[1]), .C(write[2]), ._0(opcode_2__0), ._1(opcode_2__1), ._2(opcode_2__2),
    ._3(opcode_2__3), ._4(opcode_2__4));
  registrador8bit registrador8bit_1 (.Clock(and_1_out), .load(alu_1_out), .out(registrador8bit_1_out));
  assign Out = opcode_1__4 ? registrador8bit_1_out : 8'bz;  // Driver driver_1
  and and_1 (and_1_out, Clock, opcode_2__4);
  assign Out = opcode_1__3 ? registrador8bit_2_out : 8'bz;  // Driver driver_2
  registrador8bit registrador8bit_2 (.Clock(and_2_out), .load(alu_1_out), .out(registrador8bit_2_out));
  and and_2 (and_2_out, Clock, opcode_2__3);
  assign Out = opcode_1__2 ? registrador8bit_3_out : 8'bz;  // Driver driver_3
  registrador8bit registrador8bit_3 (.Clock(and_3_out), .load(alu_1_out), .out(registrador8bit_3_out));
  and and_3 (and_3_out, Clock, opcode_2__2);
  assign Out = opcode_1__1 ? registrador8bit_4_out : 8'bz;  // Driver driver_4
  registrador8bit registrador8bit_4 (.Clock(and_4_out), .load(alu_1_out), .out(registrador8bit_4_out));
  and and_4 (and_4_out, Clock, opcode_2__1);
  registrador8bit registrador8bit_5 (.Clock(and_5_out), .load(alu_1_out), .out(registrador8bit_5_out));
  and and_5 (and_5_out, Clock, opcode_2__0);
  assign Out = opcode_1__0 ? registrador8bit_5_out : 8'bz;  // Driver driver_5
  LED led_1 (.in(Out[0]));
  LED led_2 (.in(Out[1]));
  LED led_3 (.in(Out[2]));
  LED led_4 (.in(Out[3]));
  LED OVERFLOW (.in(alu_1_overflow));
  LED a_lt_b (.in(alu_1_a_lt_b));
  LED b_lt_a (.in(alu_1_b_lt_a));
  LED a_eq_b (.in(alu_1_eq));
  LED led_5 (.in(Out[4]));
  LED led_6 (.in(Out[5]));
  LED led_7 (.in(Out[6]));
  Seven_Seg_Hex seven_seg_hex_1 (.d(Out[7:4]), .dp(1'b0));
  LED led_8 (.in(alu_1_out_7));
  LED led_9 (.in(Out[7]));
  Seven_Seg_Hex seven_seg_hex_2 (.d(Out[3:0]), .dp(1'b0));

  // Notes on the sheet:
  //   0 = soma
  //   1 = sub
  //   2 = multplicação
  //   3 = bitShift
endmodule
