// Digital circuit bitShift.dig as structural Verilog
module bitShift (
  input  [7:0] A,
  output [7:0] Y
);

  // Pins of 1 and 8 bits meet at {A[6:0], A[7]}

  assign Y = {A[6:0], A[7]};
endmodule
