// Digital circuit comparador8bit.dig as structural Verilog
module comparador8bit (
  input  CoutSub,
  input  [7:0] OutSub8bit,
  output a_lt_b,
  output b_lt_a,
  output eq
);

  wire not_1_out, or_1_out;

  not not_1 (not_1_out, CoutSub);
  or or_1 (or_1_out, OutSub8bit[0], OutSub8bit[1], OutSub8bit[2], OutSub8bit[3], OutSub8bit[4], OutSub8bit[5], OutSub8bit[6], OutSub8bit[7]);
  and and_1 (b_lt_a, not_1_out, or_1_out);
  not not_2 (eq, or_1_out);

  assign a_lt_b = CoutSub;
endmodule
