// Digital circuit fetch-cicle.dig as structural Verilog
module fetch_cicle (
  input  [26:0] in_1,
  input  [26:0] in_2,
  input  [26:0] in_3,
  input  [26:0] in_4,
  input  [26:0] in_5,
  input  RunCode,
  input  clk,
  output [7:0] out_8,
  output [26:0] out_9,
  output [26:0] out_10,
  output [26:0] out_11,
  output [26:0] out_12,
  output [26:0] out_13,
  output [26:0] out_14
);

  wire not_1_out;
  wire [26:0] relaydt_1_p4, relaydt_2_p4, relaydt_3_p4, relaydt_4_p4, relaydt_5_p4;

  registrador27bit registrador27bit_1 (.load(relaydt_1_p4), .Clock(clk), .out(out_14));
  // RelayDT #(.Bits(27)) relaydt_1: pin names not known; wires that end beside it: 1'b0, RunCode, {27{1'b0}}, relaydt_1_p4, in_1
  // RelayDT #(.Bits(27)) relaydt_2: pin names not known; wires that end beside it: 1'b0, RunCode, out_14, relaydt_2_p4, in_2
  registrador27bit registrador27bit_2 (.load(relaydt_2_p4), .Clock(clk), .out(out_13));
  registrador27bit registrador27bit_3 (.load(relaydt_3_p4), .Clock(clk), .out(out_12));
  // RelayDT #(.Bits(27)) relaydt_3: pin names not known; wires that end beside it: 1'b0, RunCode, out_13, relaydt_3_p4, in_3
  // RelayDT #(.Bits(27)) relaydt_4: pin names not known; wires that end beside it: 1'b0, RunCode, out_12, relaydt_4_p4, in_4
  registrador27bit registrador27bit_4 (.load(relaydt_4_p4), .Clock(clk), .out(out_11));
  registrador27bit registrador27bit_5 (.load(relaydt_5_p4), .Clock(clk), .out(out_10));
  // RelayDT #(.Bits(27)) relaydt_5: pin names not known; wires that end beside it: 1'b0, RunCode, out_11, relaydt_5_p4, in_5
  registrador27bit registrador27bit_6 (.load(out_10), .Clock(clk), .out(out_9));
  not not_1 (not_1_out, clk);
  instructions_27bit instructions_27bit_1 (.Clock(not_1_out), .\input (out_9), .Out(out_8));
  LED led_1 (.in(out_8[0]));
  LED led_2 (.in(out_8[1]));
  LED led_3 (.in(out_8[2]));
  LED led_4 (.in(out_8[3]));
  LED led_5 (.in(out_8[4]));
  Seven_Seg_Hex seven_seg_hex_1 (.d(out_8[7:4]), .dp(1'b0));
  LED led_6 (.in(out_8[5]));
  LED led_7 (.in(out_8[6]));
  LED led_8 (.in(out_8[7]));
  Seven_Seg_Hex seven_seg_hex_2 (.d(out_8[3:0]), .dp(1'b0));

  // Notes on the sheet:
  //   in/out, r/w, write, read, op, b, a
  //   1          1       3     3        3    8  8
  //   a - 8bit
  //   b - 8bit
  //   op - 3bit
  //   read - 3bit
  //   write - 3bit
  //   r/w - 1bit (read = 0, write = 1)
  //   a in/out - 1bit (in =1, out = 0)
  //   Op:
  //   0 = soma
  //   1 = sub
  //   2 = multplicação
  //   3 = bitShift
endmodule
