// Digital circuit instructions-27bit.dig as structural Verilog
module instructions_27bit (
  input  Clock,
  input  [26:0] \input ,
  output [7:0] Out
);

  wire and_1_out, and_2_out, not_1_out;
  wire [7:0] cpu_1_out, relaydt_1_p4;

  // RelayDT #(.Bits(8)) relaydt_1: pin names not known; wires that end beside it: \input [26], 1'b0, \input [7:0], relaydt_1_p4, Out
  and and_1 (and_1_out, Clock, \input [25]);
  CPU cpu_1 (
    .A(relaydt_1_p4), .B(\input [15:8]), .Clock(and_1_out), .read(\input [21:19]),
    .\operação (\input [18:16]), .write(\input [24:22]), .Out(cpu_1_out));
  not not_1 (not_1_out, \input [25]);
  registrador8bit registrador8bit_1 (.Clock(and_2_out), .load(cpu_1_out), .out(Out));
  and and_2 (and_2_out, not_1_out, Clock);

  // Notes on the sheet:
  //   a - 8bit
  //   b - 8bit
  //   op - 3bit
  //   read - 3bit
  //   write - 3bit
  //   r/w - 1bit (read = 0, write = 1)
  //   a in/out - 1bit (in =1, out = 0)
  //   Op:
  //   0 = soma
  //   1 = sub
  //   2 = multplicação
  //   3 = bitShift
endmodule
