// Digital circuit multiplier4bit.dig as structural Verilog
module multiplier4bit (
  input  [7:0] A4bit,
  input  [7:0] B4bit,
  output [7:0] O8bit
);

  wire sum8bit_1_cout, sum8bit_2_cout, sum8bit_3_cout;
  wire [3:0] and_3_out;
  wire [4:1] and_8_out;
  wire [5:2] and_12_out;
  wire [6:3] and_16_out;
  wire [7:0] sum8bit_1_o, sum8bit_3_o;

  and and_1 (and_3_out[0], A4bit[0], B4bit[0]);
  and and_2 (and_3_out[1], A4bit[0], B4bit[1]);
  and and_3 (and_3_out[2], A4bit[0], B4bit[2]);
  and and_4 (and_3_out[3], A4bit[0], B4bit[3]);
  sum8bit sum8bit_1 (
    .C(1'b0), .A({4'b0000, and_3_out}), .B({3'b000, and_8_out, 1'b0}), .Cout(sum8bit_1_cout), .O(sum8bit_1_o));
  and and_5 (and_8_out[1], A4bit[1], B4bit[0]);
  and and_6 (and_8_out[2], A4bit[1], B4bit[1]);
  and and_7 (and_8_out[3], A4bit[1], B4bit[2]);
  and and_8 (and_8_out[4], A4bit[1], B4bit[3]);
  and and_9 (and_12_out[2], A4bit[2], B4bit[0]);
  and and_10 (and_12_out[3], A4bit[2], B4bit[1]);
  and and_11 (and_12_out[4], A4bit[2], B4bit[2]);
  and and_12 (and_12_out[5], A4bit[2], B4bit[3]);
  sum8bit sum8bit_2 (.C(1'b0), .A(sum8bit_1_o), .B(sum8bit_3_o), .Cout(sum8bit_2_cout), .O(O8bit));
  and and_13 (and_16_out[3], A4bit[3], B4bit[0]);
  and and_14 (and_16_out[4], A4bit[3], B4bit[1]);
  and and_15 (and_16_out[5], A4bit[3], B4bit[2]);
  and and_16 (and_16_out[6], A4bit[3], B4bit[3]);
  sum8bit sum8bit_3 (
    .C(1'b0), .A({2'b00, and_12_out, 2'b00}), .B({1'b0, and_16_out, 3'b000}), .Cout(sum8bit_3_cout),
    .O(sum8bit_3_o));
  // also tied to GND on the sheet: {sum8bit_1_cout, sum8bit_2_cout, sum8bit_3_cout}
endmodule
