// Digital circuit opcode.dig as structural Verilog
module opcode (
  input  A,
  input  B,
  input  C,
  output _0,
  output _1,
  output _2,
  output _3,
  output _4
);

  wire not_1_out, not_2_out, not_3_out, not_4_out, not_5_out, not_6_out, not_7_out;

  nor nor_1 (_0, A, B, C);
  and and_1 (_1, A, not_1_out, not_2_out);
  not not_1 (not_1_out, B);
  not not_2 (not_2_out, C);
  and and_2 (_2, not_3_out, B, not_4_out);
  not not_3 (not_3_out, A);
  not not_4 (not_4_out, C);
  and and_3 (_3, A, B, not_5_out);
  not not_5 (not_5_out, C);
  and and_4 (_4, not_6_out, not_7_out, C);
  not not_6 (not_6_out, A);
  not not_7 (not_7_out, B);
endmodule
