// Digital circuit registrador27bit.dig as structural Verilog
module registrador27bit (
  input  [26:0] load,
  input  Clock,
  output [26:0] out
);

  wire [7:3] registrador8bit_4_out;

  registrador8bit registrador8bit_1 (.Clock(Clock), .load(load[7:0]), .out(out[7:0]));
  registrador8bit registrador8bit_2 (.Clock(Clock), .load(load[15:8]), .out(out[15:8]));
  registrador8bit registrador8bit_3 (.Clock(Clock), .load(load[23:16]), .out(out[23:16]));
  registrador8bit registrador8bit_4 (
    .Clock(Clock), .load({{5{1'b0}}, load[26:24]}), .out({registrador8bit_4_out, out[26:24]}));
  // also tied to GND on the sheet: {registrador8bit_4_out[3], registrador8bit_4_out[4], registrador8bit_4_out[5], registrador8bit_4_out[6], registrador8bit_4_out[7]}
endmodule
