// Digital circuit registrador8bit.dig as structural Verilog
module registrador8bit (
  input  Clock,
  input  [7:0] load,
  output [7:0] out
);

  wire not_1_out, not_2_out, not_3_out, not_4_out, not_5_out, not_6_out, not_7_out, not_8_out;

  RS_FF rs_ff_1 (.S(load[7]), .C(Clock), .R(not_1_out), .Q(out[7]));  // open: nQ
  RS_FF rs_ff_2 (.S(load[6]), .C(Clock), .R(not_2_out), .Q(out[6]));  // open: nQ
  not not_1 (not_1_out, load[7]);
  RS_FF rs_ff_3 (.S(load[5]), .C(Clock), .R(not_3_out), .Q(out[5]));  // open: nQ
  not not_2 (not_2_out, load[6]);
  RS_FF rs_ff_4 (.S(load[4]), .C(Clock), .R(not_4_out), .Q(out[4]));  // open: nQ
  not not_3 (not_3_out, load[5]);
  not not_4 (not_4_out, load[4]);
  RS_FF rs_ff_5 (.S(load[3]), .C(Clock), .R(not_5_out), .Q(out[3]));  // open: nQ
  not not_5 (not_5_out, load[3]);
  RS_FF rs_ff_6 (.S(load[2]), .C(Clock), .R(not_6_out), .Q(out[2]));  // open: nQ
  not not_6 (not_6_out, load[2]);
  RS_FF rs_ff_7 (.S(load[1]), .C(Clock), .R(not_7_out), .Q(out[1]));  // open: nQ
  not not_7 (not_7_out, load[1]);
  RS_FF rs_ff_8 (.S(load[0]), .C(Clock), .R(not_8_out), .Q(out[0]));  // open: nQ
  not not_8 (not_8_out, load[0]);
endmodule
