// Digital circuit sub1bit.dig as structural Verilog
module sub1bit (
  input  C,
  input  A,
  input  B,
  output O,
  output Cout
);

  wire and_1_out, and_2_out, not_1_out, not_2_out, xor_1_out;

  xor xor_1 (xor_1_out, A, B);
  and and_1 (and_1_out, not_1_out, B);
  not not_1 (not_1_out, A);
  xor xor_2 (O, C, xor_1_out);
  and and_2 (and_2_out, not_2_out, C);
  not not_2 (not_2_out, xor_1_out);
  or or_1 (Cout, and_2_out, and_1_out);
endmodule
