// Digital circuit sub8bit.dig as structural Verilog
module sub8bit (
  input  C,
  input  [7:0] A,
  input  [7:0] B,
  output Cout,
  output [7:0] O
);

  wire sub1bit_1_cout, sub1bit_2_cout, sub1bit_3_cout, sub1bit_4_cout, sub1bit_5_cout, sub1bit_6_cout,
       sub1bit_7_cout;

  sub1bit sub1bit_1 (.C(C), .A(A[0]), .B(B[0]), .O(O[0]), .Cout(sub1bit_1_cout));
  sub1bit sub1bit_2 (.C(sub1bit_1_cout), .A(A[1]), .B(B[1]), .O(O[1]), .Cout(sub1bit_2_cout));
  sub1bit sub1bit_3 (.C(sub1bit_2_cout), .A(A[2]), .B(B[2]), .O(O[2]), .Cout(sub1bit_3_cout));
  sub1bit sub1bit_4 (.C(sub1bit_3_cout), .A(A[3]), .B(B[3]), .O(O[3]), .Cout(sub1bit_4_cout));
  sub1bit sub1bit_5 (.C(sub1bit_4_cout), .A(A[4]), .B(B[4]), .O(O[4]), .Cout(sub1bit_5_cout));
  sub1bit sub1bit_6 (.C(sub1bit_5_cout), .A(A[5]), .B(B[5]), .O(O[5]), .Cout(sub1bit_6_cout));
  sub1bit sub1bit_7 (.C(sub1bit_6_cout), .A(A[6]), .B(B[6]), .O(O[6]), .Cout(sub1bit_7_cout));
  sub1bit sub1bit_8 (.C(sub1bit_7_cout), .A(A[7]), .B(B[7]), .O(O[7]), .Cout(Cout));
endmodule
