// Digital circuit sum1bit.dig as structural Verilog
module sum1bit (
  input  C,
  input  A,
  input  B,
  output Y,
  output X
);

  wire and_1_out, and_2_out, xor_1_out;

  xor xor_1 (xor_1_out, A, B);
  xor xor_2 (Y, C, xor_1_out);
  and and_1 (and_1_out, C, xor_1_out);
  and and_2 (and_2_out, A, B);
  or or_1 (X, and_1_out, and_2_out);
endmodule
