// Digital circuit sum8bit.dig as structural Verilog
module sum8bit (
  input  C,
  input  [7:0] A,
  input  [7:0] B,
  output Cout,
  output [7:0] O
);

  wire sum1bit_1_x, sum1bit_2_x, sum1bit_3_x, sum1bit_4_x, sum1bit_5_x, sum1bit_6_x, sum1bit_7_x;

  sum1bit sum1bit_1 (.C(C), .A(A[0]), .B(B[0]), .Y(O[0]), .X(sum1bit_1_x));
  sum1bit sum1bit_2 (.C(sum1bit_1_x), .A(A[1]), .B(B[1]), .Y(O[1]), .X(sum1bit_2_x));
  sum1bit sum1bit_3 (.C(sum1bit_2_x), .A(A[2]), .B(B[2]), .Y(O[2]), .X(sum1bit_3_x));
  sum1bit sum1bit_4 (.C(sum1bit_3_x), .A(A[3]), .B(B[3]), .Y(O[3]), .X(sum1bit_4_x));
  sum1bit sum1bit_5 (.C(sum1bit_4_x), .A(A[4]), .B(B[4]), .Y(O[4]), .X(sum1bit_5_x));
  sum1bit sum1bit_6 (.C(sum1bit_5_x), .A(A[5]), .B(B[5]), .Y(O[5]), .X(sum1bit_6_x));
  sum1bit sum1bit_7 (.C(sum1bit_6_x), .A(A[6]), .B(B[6]), .Y(O[6]), .X(sum1bit_7_x));
  sum1bit sum1bit_8 (.C(sum1bit_7_x), .A(A[7]), .B(B[7]), .Y(O[7]), .X(Cout));
endmodule
